# Fritzing sketch Untitled Sketch (saved by Fritzing 0.9.3b)

parts:
  Componente1 = Arduino Uno (Rev3)
  DRV_1 = DRV 8825 Stepper Motor Carrier, High Current [part_number="DRV 8825"]
  C1 = Capacitor Polarized [package=panasonic_d]
  DRV_2 = DRV 8825 Stepper Motor Carrier, High Current [part_number="DRV 8825"]
  C2 = Capacitor Polarized [package=panasonic_d]
  M2 = Stepper Motor - Bipolar
  M3 = Stepper Motor - Bipolar
  M4 = Stepper Motor - Bipolar
  DRV_3 = DRV 8825 Stepper Motor Carrier, High Current [part_number="DRV 8825"]
  M5 = Stepper Motor - Bipolar
  DRV_4 = DRV 8825 Stepper Motor Carrier, High Current [part_number="DRV 8825"]
  C3 = Capacitor Polarized [package=panasonic_d]
  C4 = Capacitor Polarized [package=panasonic_d]
  Power_plug1 = Power plug
  Power_plug2 = Power plug  # not connected

nets:
  GND: Componente1.GND, DRV_1.GROUND_ST/_MT, DRV_1.GROUND_LOG, C1.-, DRV_2.GROUND_ST/_MT, DRV_2.VOLTAGE_DD, DRV_2.GROUND_LOG, C2.-, DRV_3.GROUND_ST/_MT, DRV_3.GROUND_LOG, DRV_4.GROUND_ST/_MT, DRV_4.GROUND_LOG, C3.-, C4.-, Power_plug1.GND
  N1: Componente1.D2, DRV_4.STEP
  N2: Componente1.D3_PWM, DRV_2.STEP
  N3: Componente1.D4, DRV_1.STEP
  N4: Componente1.D5_PWM, DRV_4.DIRECTION
  N5: Componente1.D6_PWM, DRV_2.DIRECTION
  N6: Componente1.D7, DRV_1.DIRECTION
  N7: Componente1.5V, DRV_1.RESET, DRV_1.SLEEP, DRV_4.RESET, DRV_4.SLEEP
  8V: DRV_1.VOLTAGE_ST/_MT, C1.+, DRV_2.VOLTAGE_ST/_MT, C2.+, DRV_3.VOLTAGE_ST/_MT, DRV_4.VOLTAGE_ST/_MT, C3.+, C4.+, Power_plug1.VCC
  N8: DRV_1.OUT_2B, M5.A
  N9: DRV_1.OUT_2A, M5.C
  N10: DRV_1.OUT_1A, M5.B
  N11: DRV_1.OUT_1B, M5.D
  N12: DRV_1.VOLTAGE_DD, DRV_3.VOLTAGE_DD, DRV_4.VOLTAGE_DD
  N13: DRV_2.RESET, DRV_2.SLEEP
  N14: DRV_2.OUT_2B, M2.A
  N15: DRV_2.OUT_2A, M2.C
  N16: DRV_2.OUT_1A, M2.B
  N17: DRV_2.OUT_1B, M2.D
  N18: M3.A, DRV_3.OUT_2B
  N19: M3.C, DRV_3.OUT_2A
  N20: M3.B, DRV_3.OUT_1A
  N21: M3.D, DRV_3.OUT_1B
  N22: M4.A, DRV_4.OUT_2B
  N23: M4.C, DRV_4.OUT_2A
  N24: M4.B, DRV_4.OUT_1A
  N25: M4.D, DRV_4.OUT_1B
  N26: DRV_3.ENABLE, DRV_4.ENABLE
  N27: DRV_3.RESET, DRV_3.SLEEP
